// Logisim project Processador.circ as structural Verilog
module registrador_4bit (
  input  clock,
  input  _3_pos_bit,
  input  _2_pos_bit,
  input  _1_pos_bit,
  input  _0_pos_bit,
  output _3_pos_bit_2,
  output _2_pos_bit_2,
  output _1_pos_bit_2,
  output _0_pos_bit_2
);

  D_Flip_Flop d_ff_1 (.clk(clock), .D(_3_pos_bit), .Q(_3_pos_bit_2));  // open: Qn, preset, en, reset
  D_Flip_Flop d_ff_2 (.clk(clock), .D(_2_pos_bit), .Q(_2_pos_bit_2));  // open: Qn, preset, en, reset
  D_Flip_Flop d_ff_3 (.clk(clock), .D(_1_pos_bit), .Q(_1_pos_bit_2));  // open: Qn, preset, en, reset
  D_Flip_Flop d_ff_4 (.clk(clock), .D(_0_pos_bit), .Q(_0_pos_bit_2));  // open: Qn, preset, en, reset
endmodule

module registrador_8bit (
  input  clock,
  input  _7_pos_bit,
  input  _6_pos_bit,
  input  _5_pos_bit,
  input  _4_pos_bit,
  input  _3_pos_bit,
  input  _2_pos_bit,
  input  _1_pos_bit,
  input  _0_pos_bit,
  output _7_pos_bit_2,
  output _6_pos_bit_2,
  output _5_pos_bit_2,
  output _4_pos_bit_2,
  output _3_pos_bit_2,
  output _2_pos_bit_2,
  output _1_pos_bit_2,
  output _0_pos_bit_2
);

  registrador_4bit registrador_4bit_1 (
    .clock(clock), ._3_pos_bit(_7_pos_bit), ._2_pos_bit(_6_pos_bit), ._1_pos_bit(_5_pos_bit),
    ._0_pos_bit(_4_pos_bit), ._3_pos_bit_2(_7_pos_bit_2), ._2_pos_bit_2(_6_pos_bit_2),
    ._1_pos_bit_2(_5_pos_bit_2), ._0_pos_bit_2(_4_pos_bit_2));
  registrador_4bit registrador_4bit_2 (
    .clock(clock), ._3_pos_bit(_3_pos_bit), ._2_pos_bit(_2_pos_bit), ._1_pos_bit(_1_pos_bit),
    ._0_pos_bit(_0_pos_bit), ._3_pos_bit_2(_3_pos_bit_2), ._2_pos_bit_2(_2_pos_bit_2),
    ._1_pos_bit_2(_1_pos_bit_2), ._0_pos_bit_2(_0_pos_bit_2));
endmodule

module Registrador_de_instrucao (
  input  clock,
  input  _7_pos_bit,
  input  _6_pos_bit,
  input  _5_pos_bit,
  input  _4_pos_bit,
  input  _3_pos_bit,
  input  _2_pos_bit,
  input  _1_pos_bit,
  input  _0_pos_bit,
  output op1,
  output op0,
  output R1_2,
  output R1_1,
  output R1_0,
  output X_2,
  output X_1,
  output X_0
);

  registrador_8bit registrador_8bit_1 (
    .clock(clock), ._7_pos_bit(_7_pos_bit), ._6_pos_bit(_6_pos_bit), ._5_pos_bit(_5_pos_bit),
    ._4_pos_bit(_4_pos_bit), ._3_pos_bit(_3_pos_bit), ._2_pos_bit(_2_pos_bit), ._1_pos_bit(_1_pos_bit),
    ._0_pos_bit(_0_pos_bit), ._7_pos_bit_2(op1), ._6_pos_bit_2(op0), ._5_pos_bit_2(R1_2),
    ._4_pos_bit_2(R1_1), ._3_pos_bit_2(R1_0), ._2_pos_bit_2(X_2), ._1_pos_bit_2(X_1), ._0_pos_bit_2(X_0));
endmodule

module Banco_de_registradores (
  input  r1_2,
  input  r1_1,
  input  r1_0,
  input  Clock,
  output _3,
  output _2,
  output _1,
  output _0
);

  wire R0__0_pos_bit_2, R0__1_pos_bit_2, R0__2_pos_bit_2, R0__3_pos_bit_2, R1__0_pos_bit_2, R1__1_pos_bit_2,
       R1__2_pos_bit_2, R1__3_pos_bit_2, R2__0_pos_bit_2, R2__1_pos_bit_2, R2__2_pos_bit_2, R2__3_pos_bit_2,
       R3__0_pos_bit_2, R3__1_pos_bit_2, R3__2_pos_bit_2, R3__3_pos_bit_2, R4__0_pos_bit_2, R4__1_pos_bit_2,
       R4__2_pos_bit_2, R4__3_pos_bit_2, R5__0_pos_bit_2, R5__1_pos_bit_2, R5__2_pos_bit_2, R5__3_pos_bit_2,
       R6__0_pos_bit_2, R6__1_pos_bit_2, R6__2_pos_bit_2, R6__3_pos_bit_2, R7__0_pos_bit_2, R7__1_pos_bit_2,
       R7__2_pos_bit_2, R7__3_pos_bit_2;

  registrador_4bit R0 (
    .clock(Clock), ._3_pos_bit_2(R0__3_pos_bit_2), ._2_pos_bit_2(R0__2_pos_bit_2),
    ._1_pos_bit_2(R0__1_pos_bit_2), ._0_pos_bit_2(R0__0_pos_bit_2));  // open: _3_pos_bit, _2_pos_bit, _1_pos_bit, _0_pos_bit
  registrador_4bit R1 (
    .clock(Clock), ._0_pos_bit(1'b1), ._3_pos_bit_2(R1__3_pos_bit_2), ._2_pos_bit_2(R1__2_pos_bit_2),
    ._1_pos_bit_2(R1__1_pos_bit_2), ._0_pos_bit_2(R1__0_pos_bit_2));  // open: _3_pos_bit, _2_pos_bit, _1_pos_bit
  registrador_4bit R2 (
    .clock(Clock), ._1_pos_bit(1'b1), ._3_pos_bit_2(R2__3_pos_bit_2), ._2_pos_bit_2(R2__2_pos_bit_2),
    ._1_pos_bit_2(R2__1_pos_bit_2), ._0_pos_bit_2(R2__0_pos_bit_2));  // open: _3_pos_bit, _2_pos_bit, _0_pos_bit
  registrador_4bit R3 (
    .clock(Clock), ._1_pos_bit(1'b1), ._0_pos_bit(1'b1), ._3_pos_bit_2(R3__3_pos_bit_2),
    ._2_pos_bit_2(R3__2_pos_bit_2), ._1_pos_bit_2(R3__1_pos_bit_2), ._0_pos_bit_2(R3__0_pos_bit_2));  // open: _3_pos_bit, _2_pos_bit
  Multiplexador_8_1 u__3 (
    .control0(r1_0), .control1(r1_1), .control2(r1_2), .a(R0__3_pos_bit_2), .b(R1__3_pos_bit_2),
    .c(R2__3_pos_bit_2), .d(R3__3_pos_bit_2), .e(R4__3_pos_bit_2), .f(R5__3_pos_bit_2), .g(R6__3_pos_bit_2),
    .h(R7__3_pos_bit_2), .out_12(_3));
  Multiplexador_8_1 u__2 (
    .control0(r1_0), .control1(r1_1), .control2(r1_2), .a(R0__2_pos_bit_2), .b(R1__2_pos_bit_2),
    .c(R2__2_pos_bit_2), .d(R3__2_pos_bit_2), .e(R4__2_pos_bit_2), .f(R5__2_pos_bit_2), .g(R6__2_pos_bit_2),
    .h(R7__2_pos_bit_2), .out_12(_2));
  Multiplexador_8_1 u__1 (
    .control0(r1_0), .control1(r1_1), .control2(r1_2), .a(R0__1_pos_bit_2), .b(R1__1_pos_bit_2),
    .c(R2__1_pos_bit_2), .d(R3__1_pos_bit_2), .e(R4__1_pos_bit_2), .f(R5__1_pos_bit_2), .g(R6__1_pos_bit_2),
    .h(R7__1_pos_bit_2), .out_12(_1));
  Multiplexador_8_1 u__0 (
    .control0(r1_0), .control1(r1_1), .control2(r1_2), .a(R0__0_pos_bit_2), .b(R1__0_pos_bit_2),
    .c(R2__0_pos_bit_2), .d(R3__0_pos_bit_2), .e(R4__0_pos_bit_2), .f(R5__0_pos_bit_2), .g(R6__0_pos_bit_2),
    .h(R7__0_pos_bit_2), .out_12(_0));
  registrador_4bit R4 (
    .clock(Clock), ._2_pos_bit(1'b1), ._3_pos_bit_2(R4__3_pos_bit_2), ._2_pos_bit_2(R4__2_pos_bit_2),
    ._1_pos_bit_2(R4__1_pos_bit_2), ._0_pos_bit_2(R4__0_pos_bit_2));  // open: _3_pos_bit, _1_pos_bit, _0_pos_bit
  registrador_4bit R5 (
    .clock(Clock), ._2_pos_bit(1'b1), ._0_pos_bit(1'b1), ._3_pos_bit_2(R5__3_pos_bit_2),
    ._2_pos_bit_2(R5__2_pos_bit_2), ._1_pos_bit_2(R5__1_pos_bit_2), ._0_pos_bit_2(R5__0_pos_bit_2));  // open: _3_pos_bit, _1_pos_bit
  registrador_4bit R6 (
    .clock(Clock), ._2_pos_bit(1'b1), ._1_pos_bit(1'b1), ._3_pos_bit_2(R6__3_pos_bit_2),
    ._2_pos_bit_2(R6__2_pos_bit_2), ._1_pos_bit_2(R6__1_pos_bit_2), ._0_pos_bit_2(R6__0_pos_bit_2));  // open: _3_pos_bit, _0_pos_bit
  registrador_4bit R7 (
    .clock(Clock), ._2_pos_bit(1'b1), ._1_pos_bit(1'b1), ._0_pos_bit(1'b1), ._3_pos_bit_2(R7__3_pos_bit_2),
    ._2_pos_bit_2(R7__2_pos_bit_2), ._1_pos_bit_2(R7__1_pos_bit_2), ._0_pos_bit_2(R7__0_pos_bit_2));  // open: _3_pos_bit
endmodule

module Multiplexador_2_1 (
  input  control,
  input  A,
  input  B,
  output out_4
);

  wire and_1_out, and_2_out, not_1_out;

  not not_1 (not_1_out, control);
  and and_1 (and_1_out, not_1_out, A);
  or or_1 (out_4, and_1_out, and_2_out);
  and and_2 (and_2_out, B, control);
endmodule

module Multiplexador_4_1 (
  input  control0,
  input  control1,
  input  a,
  input  b,
  input  c,
  input  d,
  output out_7
);

  wire multiplexador_2_1_1_out_4, multiplexador_2_1_2_out_4;

  Multiplexador_2_1 multiplexador_2_1_1 (.control(control0), .A(a), .B(b), .out_4(multiplexador_2_1_1_out_4));
  Multiplexador_2_1 multiplexador_2_1_2 (.control(control0), .A(c), .B(d), .out_4(multiplexador_2_1_2_out_4));
  Multiplexador_2_1 multiplexador_2_1_3 (
    .control(control1), .A(multiplexador_2_1_1_out_4), .B(multiplexador_2_1_2_out_4), .out_4(out_7));
endmodule

module Multiplexador_8_1 (
  input  control0,
  input  control1,
  input  control2,
  input  a,
  input  b,
  input  c,
  input  d,
  input  e,
  input  f,
  input  g,
  input  h,
  output out_12
);

  wire multiplexador_4_1_1_out_7, multiplexador_4_1_2_out_7;

  Multiplexador_4_1 multiplexador_4_1_1 (
    .control0(control0), .control1(control1), .a(a), .b(b), .c(c), .d(d), .out_7(multiplexador_4_1_1_out_7));
  Multiplexador_2_1 multiplexador_2_1_1 (
    .control(control2), .A(multiplexador_4_1_1_out_7), .B(multiplexador_4_1_2_out_7), .out_4(out_12));
  Multiplexador_4_1 multiplexador_4_1_2 (
    .control0(control0), .control1(control1), .a(e), .b(f), .c(g), .d(h), .out_7(multiplexador_4_1_2_out_7));
endmodule
